// Digital circuit ECM-16 computer.dig as structural Verilog
module ECM_16_computer (
  input  Clk,
  input  [31:0] DMA_Addr,
  input  [7:0] in_3,
  input  DMA_RQ
);

  wire and_2_out, and_3_out, and_5_out, and_6_out, Byte, C_out, clk_stop, clk_t, Cont_out, d_ff_1_nq,
       d_ff_1_q, d_ff_as_1_nq, d_ff_as_1_q, d_ff_as_2_nq, d_ff_as_2_q, iAck, Int_mock_out, Int_q,
       multiplexer_1_out, not_1_out, not_2_out, not_3_out, not_4_out, not_5_out, not_6_out, not_7_out,
       not_8_out, not_9_out, not_10_out, nr, or_1_out, or_2_out, or_3_out, R_out, read, RST, S_out, Soft_Int,
       Stop_out, write;
  wire [3:0] SR_disp;
  wire [8:0] en;
  wire [9:0] latch;
  wire [15:0] ecm_16_cpu_1_data, IR_disp, MDB_disp, ROM_d, sel, states;
  wire [31:0] Addr_disp, BP, ecm_16_cpu_1_address, FP, IV_disp, MAB_disp, PC, SP;
  wire [63:0] R0_3, R4_7;

  not not_1 (not_1_out, RST);
  Button #(.activeLow("true")) R (.out(R_out));
  and and_1 (nr, not_1_out, R_out);
  LED led_1 (.in(IR_disp[15]));
  LED led_2 (.in(IR_disp[14]));
  LED led_3 (.in(R0_3[15]));
  LED led_4 (.in(R0_3[14]));
  LED led_5 (.in(R0_3[31]));
  LED led_6 (.in(R0_3[30]));
  LED led_7 (.in(R0_3[47]));
  LED led_8 (.in(R0_3[46]));
  LED led_9 (.in(R0_3[63]));
  LED led_10 (.in(R0_3[62]));
  LED led_11 (.in(R4_7[15]));
  LED led_12 (.in(R4_7[14]));
  LED led_13 (.in(R4_7[31]));
  LED led_14 (.in(R4_7[30]));
  LED led_15 (.in(R4_7[47]));
  LED led_16 (.in(R4_7[46]));
  LED led_17 (.in(R4_7[63]));
  LED led_18 (.in(R4_7[62]));
  LED led_19 (.in(MDB_disp[15]));
  LED led_20 (.in(MDB_disp[14]));
  not not_2 (not_2_out, nr);
  Button Cont (.out(Cont_out));
  LED led_21 (.in(IR_disp[13]));
  LED led_22 (.in(IR_disp[12]));
  LED led_23 (.in(IR_disp[11]));
  LED led_24 (.in(IR_disp[10]));
  LED led_25 (.in(R0_3[13]));
  LED led_26 (.in(R0_3[12]));
  LED led_27 (.in(R0_3[11]));
  LED led_28 (.in(R0_3[10]));
  LED led_29 (.in(R0_3[29]));
  LED led_30 (.in(R0_3[28]));
  LED led_31 (.in(R0_3[27]));
  LED led_32 (.in(R0_3[26]));
  LED led_33 (.in(R0_3[45]));
  LED led_34 (.in(R0_3[44]));
  LED led_35 (.in(R0_3[43]));
  LED led_36 (.in(R0_3[42]));
  LED led_37 (.in(R0_3[61]));
  LED led_38 (.in(R0_3[60]));
  LED led_39 (.in(R0_3[59]));
  LED led_40 (.in(R0_3[58]));
  LED led_41 (.in(R4_7[13]));
  LED led_42 (.in(R4_7[12]));
  LED led_43 (.in(R4_7[11]));
  LED led_44 (.in(R4_7[10]));
  LED led_45 (.in(R4_7[29]));
  LED led_46 (.in(R4_7[28]));
  LED led_47 (.in(R4_7[27]));
  LED led_48 (.in(R4_7[26]));
  LED led_49 (.in(R4_7[45]));
  LED led_50 (.in(R4_7[44]));
  LED led_51 (.in(R4_7[43]));
  LED led_52 (.in(R4_7[42]));
  LED led_53 (.in(R4_7[61]));
  LED led_54 (.in(R4_7[60]));
  LED led_55 (.in(R4_7[59]));
  LED led_56 (.in(R4_7[58]));
  LED led_57 (.in(MDB_disp[13]));
  LED led_58 (.in(MDB_disp[12]));
  LED led_59 (.in(MDB_disp[11]));
  LED led_60 (.in(MDB_disp[10]));
  LED led_61 (.in(IR_disp[9]));
  LED led_62 (.in(IR_disp[8]));
  LED led_63 (.in(IR_disp[7]));
  LED led_64 (.in(IR_disp[6]));
  LED led_65 (.in(R0_3[9]));
  LED led_66 (.in(R0_3[8]));
  LED led_67 (.in(R0_3[7]));
  LED led_68 (.in(R0_3[6]));
  LED led_69 (.in(R0_3[25]));
  LED led_70 (.in(R0_3[24]));
  LED led_71 (.in(R0_3[23]));
  LED led_72 (.in(R0_3[22]));
  LED led_73 (.in(R0_3[41]));
  LED led_74 (.in(R0_3[40]));
  LED led_75 (.in(R0_3[39]));
  LED led_76 (.in(R0_3[38]));
  LED led_77 (.in(R0_3[57]));
  LED led_78 (.in(R0_3[56]));
  LED led_79 (.in(R0_3[55]));
  LED led_80 (.in(R0_3[54]));
  LED led_81 (.in(R4_7[9]));
  LED led_82 (.in(R4_7[8]));
  LED led_83 (.in(R4_7[7]));
  LED led_84 (.in(R4_7[6]));
  LED led_85 (.in(R4_7[25]));
  LED led_86 (.in(R4_7[24]));
  LED led_87 (.in(R4_7[23]));
  LED led_88 (.in(R4_7[22]));
  LED led_89 (.in(R4_7[41]));
  LED led_90 (.in(R4_7[40]));
  LED led_91 (.in(R4_7[39]));
  LED led_92 (.in(R4_7[38]));
  LED led_93 (.in(R4_7[57]));
  LED led_94 (.in(R4_7[56]));
  LED led_95 (.in(R4_7[55]));
  LED led_96 (.in(R4_7[54]));
  LED led_97 (.in(MDB_disp[9]));
  LED led_98 (.in(MDB_disp[8]));
  LED led_99 (.in(MDB_disp[7]));
  LED led_100 (.in(MDB_disp[6]));
  Button Stop (.out(Stop_out));
  or or_1 (or_1_out, not_2_out, Cont_out);
  LED led_101 (.in(IR_disp[5]));
  LED led_102 (.in(IR_disp[4]));
  LED led_103 (.in(IR_disp[3]));
  LED led_104 (.in(IR_disp[2]));
  LED led_105 (.in(R0_3[5]));
  LED led_106 (.in(R0_3[4]));
  LED led_107 (.in(R0_3[3]));
  LED led_108 (.in(R0_3[2]));
  LED led_109 (.in(R0_3[21]));
  LED led_110 (.in(R0_3[20]));
  LED led_111 (.in(R0_3[19]));
  LED led_112 (.in(R0_3[18]));
  LED led_113 (.in(R0_3[37]));
  LED led_114 (.in(R0_3[36]));
  LED led_115 (.in(R0_3[35]));
  LED led_116 (.in(R0_3[34]));
  LED led_117 (.in(R0_3[53]));
  LED led_118 (.in(R0_3[52]));
  LED led_119 (.in(R0_3[51]));
  LED led_120 (.in(R0_3[50]));
  LED led_121 (.in(R4_7[5]));
  LED led_122 (.in(R4_7[4]));
  LED led_123 (.in(R4_7[3]));
  LED led_124 (.in(R4_7[2]));
  LED led_125 (.in(R4_7[21]));
  LED led_126 (.in(R4_7[20]));
  LED led_127 (.in(R4_7[19]));
  LED led_128 (.in(R4_7[18]));
  LED led_129 (.in(R4_7[37]));
  LED led_130 (.in(R4_7[36]));
  LED led_131 (.in(R4_7[35]));
  LED led_132 (.in(R4_7[34]));
  LED led_133 (.in(R4_7[53]));
  LED led_134 (.in(R4_7[52]));
  LED led_135 (.in(R4_7[51]));
  LED led_136 (.in(R4_7[50]));
  LED led_137 (.in(MDB_disp[5]));
  LED led_138 (.in(MDB_disp[4]));
  LED led_139 (.in(MDB_disp[3]));
  LED led_140 (.in(MDB_disp[2]));
  or or_2 (or_2_out, Stop_out, clk_stop);
  not not_3 (not_3_out, or_1_out);
  LED led_141 (.in(IR_disp[1]));
  LED led_142 (.in(IR_disp[0]));
  LED led_143 (.in(R0_3[1]));
  LED led_144 (.in(R0_3[0]));
  LED led_145 (.in(R0_3[17]));
  LED led_146 (.in(R0_3[16]));
  LED led_147 (.in(R0_3[33]));
  LED led_148 (.in(R0_3[32]));
  LED led_149 (.in(R0_3[49]));
  LED led_150 (.in(R0_3[48]));
  LED led_151 (.in(R4_7[1]));
  LED led_152 (.in(R4_7[0]));
  LED led_153 (.in(R4_7[17]));
  LED led_154 (.in(R4_7[16]));
  LED led_155 (.in(R4_7[33]));
  LED led_156 (.in(R4_7[32]));
  LED led_157 (.in(R4_7[49]));
  LED led_158 (.in(R4_7[48]));
  LED led_159 (.in(MDB_disp[1]));
  LED led_160 (.in(MDB_disp[0]));
  and and_2 (and_2_out, or_2_out, not_3_out);
  Button C (.out(C_out));
  Button S (.out(S_out));
  LED led_161 (.in(SR_disp[0]));
  LED led_162 (.in(SR_disp[1]));
  LED led_163 (.in(SR_disp[2]));
  LED led_164 (.in(SR_disp[3]));
  D_FF_AS d_ff_as_1 (.Set(1'b0), .D(d_ff_as_1_nq), .C(S_out), .Clr(1'b0), .Q(d_ff_as_1_q), .nQ(d_ff_as_1_nq));
  LED led_165 (.in(PC[31]));
  LED led_166 (.in(SP[31]));
  LED led_167 (.in(FP[31]));
  LED led_168 (.in(BP[31]));
  LED led_169 (.in(MAB_disp[31]));
  LED led_170 (.in(Addr_disp[31]));
  LED led_171 (.in(IV_disp[31]));
  D_FF_AS d_ff_as_2 (.Set(1'b0), .D(and_2_out), .C(d_ff_1_q), .Clr(or_1_out), .Q(d_ff_as_2_q), .nQ(d_ff_as_2_nq));
  Multiplexer multiplexer_1 (.sel(d_ff_as_1_q), .in_0(C_out), .in_1(Clk), .out(multiplexer_1_out));
  LED led_172 (.in(PC[30]));
  LED led_173 (.in(PC[29]));
  LED led_174 (.in(PC[28]));
  LED led_175 (.in(PC[27]));
  LED led_176 (.in(SP[30]));
  LED led_177 (.in(SP[29]));
  LED led_178 (.in(SP[28]));
  LED led_179 (.in(SP[27]));
  LED led_180 (.in(FP[30]));
  LED led_181 (.in(FP[29]));
  LED led_182 (.in(FP[28]));
  LED led_183 (.in(FP[27]));
  LED led_184 (.in(BP[30]));
  LED led_185 (.in(BP[29]));
  LED led_186 (.in(BP[28]));
  LED led_187 (.in(BP[27]));
  LED led_188 (.in(MAB_disp[30]));
  LED led_189 (.in(MAB_disp[29]));
  LED led_190 (.in(MAB_disp[28]));
  LED led_191 (.in(MAB_disp[27]));
  LED led_192 (.in(Addr_disp[30]));
  LED led_193 (.in(Addr_disp[29]));
  LED led_194 (.in(Addr_disp[28]));
  LED led_195 (.in(Addr_disp[27]));
  LED led_196 (.in(IV_disp[30]));
  LED led_197 (.in(IV_disp[29]));
  LED led_198 (.in(IV_disp[28]));
  LED led_199 (.in(IV_disp[27]));
  LED led_200 (.in(d_ff_as_2_q));
  LED led_201 (.in(PC[26]));
  LED led_202 (.in(PC[25]));
  LED led_203 (.in(PC[24]));
  LED led_204 (.in(PC[23]));
  LED led_205 (.in(SP[26]));
  LED led_206 (.in(SP[25]));
  LED led_207 (.in(SP[24]));
  LED led_208 (.in(SP[23]));
  LED led_209 (.in(FP[26]));
  LED led_210 (.in(FP[25]));
  LED led_211 (.in(FP[24]));
  LED led_212 (.in(FP[23]));
  LED led_213 (.in(BP[26]));
  LED led_214 (.in(BP[25]));
  LED led_215 (.in(BP[24]));
  LED led_216 (.in(BP[23]));
  LED led_217 (.in(MAB_disp[26]));
  LED led_218 (.in(MAB_disp[25]));
  LED led_219 (.in(MAB_disp[24]));
  LED led_220 (.in(MAB_disp[23]));
  LED led_221 (.in(Addr_disp[26]));
  LED led_222 (.in(Addr_disp[25]));
  LED led_223 (.in(Addr_disp[24]));
  LED led_224 (.in(Addr_disp[23]));
  LED led_225 (.in(IV_disp[26]));
  LED led_226 (.in(IV_disp[25]));
  LED led_227 (.in(IV_disp[24]));
  LED led_228 (.in(IV_disp[23]));
  and and_3 (and_3_out, d_ff_as_2_nq, multiplexer_1_out);
  LED led_229 (.in(PC[22]));
  LED led_230 (.in(PC[21]));
  LED led_231 (.in(PC[20]));
  LED led_232 (.in(PC[19]));
  LED led_233 (.in(SP[22]));
  LED led_234 (.in(SP[21]));
  LED led_235 (.in(SP[20]));
  LED led_236 (.in(SP[19]));
  LED led_237 (.in(FP[22]));
  LED led_238 (.in(FP[21]));
  LED led_239 (.in(FP[20]));
  LED led_240 (.in(FP[19]));
  LED led_241 (.in(BP[22]));
  LED led_242 (.in(BP[21]));
  LED led_243 (.in(BP[20]));
  LED led_244 (.in(BP[19]));
  LED led_245 (.in(MAB_disp[22]));
  LED led_246 (.in(MAB_disp[21]));
  LED led_247 (.in(MAB_disp[20]));
  LED led_248 (.in(MAB_disp[19]));
  LED led_249 (.in(Addr_disp[22]));
  LED led_250 (.in(Addr_disp[21]));
  LED led_251 (.in(Addr_disp[20]));
  LED led_252 (.in(Addr_disp[19]));
  LED led_253 (.in(IV_disp[22]));
  LED led_254 (.in(IV_disp[21]));
  LED led_255 (.in(IV_disp[20]));
  LED led_256 (.in(IV_disp[19]));
  D_FF d_ff_1 (.D(d_ff_1_nq), .C(and_3_out), .Q(d_ff_1_q), .nQ(d_ff_1_nq));
  LED led_257 (.in(PC[15]));
  LED led_258 (.in(PC[18]));
  LED led_259 (.in(PC[17]));
  LED led_260 (.in(PC[16]));
  LED led_261 (.in(SP[15]));
  LED led_262 (.in(SP[18]));
  LED led_263 (.in(SP[17]));
  LED led_264 (.in(SP[16]));
  LED led_265 (.in(FP[15]));
  LED led_266 (.in(FP[18]));
  LED led_267 (.in(FP[17]));
  LED led_268 (.in(FP[16]));
  LED led_269 (.in(BP[15]));
  LED led_270 (.in(BP[18]));
  LED led_271 (.in(BP[17]));
  LED led_272 (.in(BP[16]));
  LED led_273 (.in(MAB_disp[15]));
  LED led_274 (.in(MAB_disp[18]));
  LED led_275 (.in(MAB_disp[17]));
  LED led_276 (.in(MAB_disp[16]));
  LED led_277 (.in(Addr_disp[15]));
  LED led_278 (.in(Addr_disp[18]));
  LED led_279 (.in(Addr_disp[17]));
  LED led_280 (.in(Addr_disp[16]));
  LED led_281 (.in(IV_disp[15]));
  LED led_282 (.in(IV_disp[18]));
  LED led_283 (.in(IV_disp[17]));
  LED led_284 (.in(IV_disp[16]));
  LED led_285 (.in(PC[14]));
  LED led_286 (.in(PC[13]));
  LED led_287 (.in(PC[12]));
  LED led_288 (.in(PC[11]));
  LED led_289 (.in(SP[14]));
  LED led_290 (.in(SP[13]));
  LED led_291 (.in(SP[12]));
  LED led_292 (.in(SP[11]));
  LED led_293 (.in(FP[14]));
  LED led_294 (.in(FP[13]));
  LED led_295 (.in(FP[12]));
  LED led_296 (.in(FP[11]));
  LED led_297 (.in(BP[14]));
  LED led_298 (.in(BP[13]));
  LED led_299 (.in(BP[12]));
  LED led_300 (.in(BP[11]));
  LED led_301 (.in(MAB_disp[14]));
  LED led_302 (.in(MAB_disp[13]));
  LED led_303 (.in(MAB_disp[12]));
  LED led_304 (.in(MAB_disp[11]));
  LED led_305 (.in(Addr_disp[14]));
  LED led_306 (.in(Addr_disp[13]));
  LED led_307 (.in(Addr_disp[12]));
  LED led_308 (.in(Addr_disp[11]));
  LED led_309 (.in(IV_disp[14]));
  LED led_310 (.in(IV_disp[13]));
  LED led_311 (.in(IV_disp[12]));
  LED led_312 (.in(IV_disp[11]));
  and and_4 (clk_t, not_4_out, d_ff_1_q);
  not not_4 (not_4_out, DMA_RQ);
  not not_5 (not_5_out, d_ff_1_q);
  LED led_313 (.in(PC[10]));
  LED led_314 (.in(PC[9]));
  LED led_315 (.in(PC[8]));
  LED led_316 (.in(PC[7]));
  LED led_317 (.in(SP[10]));
  LED led_318 (.in(SP[9]));
  LED led_319 (.in(SP[8]));
  LED led_320 (.in(SP[7]));
  LED led_321 (.in(FP[10]));
  LED led_322 (.in(FP[9]));
  LED led_323 (.in(FP[8]));
  LED led_324 (.in(FP[7]));
  LED led_325 (.in(BP[10]));
  LED led_326 (.in(BP[9]));
  LED led_327 (.in(BP[8]));
  LED led_328 (.in(BP[7]));
  LED led_329 (.in(MAB_disp[10]));
  LED led_330 (.in(MAB_disp[9]));
  LED led_331 (.in(MAB_disp[8]));
  LED led_332 (.in(MAB_disp[7]));
  LED led_333 (.in(Addr_disp[10]));
  LED led_334 (.in(Addr_disp[9]));
  LED led_335 (.in(Addr_disp[8]));
  LED led_336 (.in(Addr_disp[7]));
  LED led_337 (.in(IV_disp[10]));
  LED led_338 (.in(IV_disp[9]));
  LED led_339 (.in(IV_disp[8]));
  LED led_340 (.in(IV_disp[7]));
  LED led_341 (.in(PC[6]));
  LED led_342 (.in(PC[5]));
  LED led_343 (.in(PC[4]));
  LED led_344 (.in(PC[3]));
  LED led_345 (.in(SP[6]));
  LED led_346 (.in(SP[5]));
  LED led_347 (.in(SP[4]));
  LED led_348 (.in(SP[3]));
  LED led_349 (.in(FP[6]));
  LED led_350 (.in(FP[5]));
  LED led_351 (.in(FP[4]));
  LED led_352 (.in(FP[3]));
  LED led_353 (.in(BP[6]));
  LED led_354 (.in(BP[5]));
  LED led_355 (.in(BP[4]));
  LED led_356 (.in(BP[3]));
  LED led_357 (.in(MAB_disp[6]));
  LED led_358 (.in(MAB_disp[5]));
  LED led_359 (.in(MAB_disp[4]));
  LED led_360 (.in(MAB_disp[3]));
  LED led_361 (.in(Addr_disp[6]));
  LED led_362 (.in(Addr_disp[5]));
  LED led_363 (.in(Addr_disp[4]));
  LED led_364 (.in(Addr_disp[3]));
  LED led_365 (.in(IV_disp[6]));
  LED led_366 (.in(IV_disp[5]));
  LED led_367 (.in(IV_disp[4]));
  LED led_368 (.in(IV_disp[3]));
  LED u_clk (.in(clk_t));
  LED nclk (.in(not_5_out));
  Button Int_mock (.out(Int_mock_out));
  LED led_369 (.in(PC[2]));
  LED led_370 (.in(PC[1]));
  LED led_371 (.in(PC[0]));
  LED led_372 (.in(SP[2]));
  LED led_373 (.in(SP[1]));
  LED led_374 (.in(SP[0]));
  LED led_375 (.in(FP[2]));
  LED led_376 (.in(FP[1]));
  LED led_377 (.in(FP[0]));
  LED led_378 (.in(BP[2]));
  LED led_379 (.in(BP[1]));
  LED led_380 (.in(BP[0]));
  LED led_381 (.in(MAB_disp[2]));
  LED led_382 (.in(MAB_disp[1]));
  LED led_383 (.in(MAB_disp[0]));
  LED led_384 (.in(Addr_disp[2]));
  LED led_385 (.in(Addr_disp[1]));
  LED led_386 (.in(Addr_disp[0]));
  LED led_387 (.in(IV_disp[2]));
  LED led_388 (.in(IV_disp[1]));
  LED led_389 (.in(IV_disp[0]));
  not not_6 (not_6_out, iAck);
  or or_3 (or_3_out, Soft_Int, Int_mock_out);
  not not_7 (not_7_out, not_6_out);
  not not_8 (not_8_out, or_3_out);
  and and_5 (and_5_out, not_6_out, not_7_out);
  not not_9 (not_9_out, not_8_out);
  ECM_16_CPU ecm_16_cpu_1 (
    .iN(in_3), .IRQ(Int_q), .soft_int(Soft_Int), .iAck(iAck), .DMA_addr(DMA_Addr), .DMA_RQ(DMA_RQ), .nR(nr),
    .clk(clk_t), .RST(RST), .clk_stp(clk_stop), .read(read), .write(write), .\byte (Byte),
    .Data(ecm_16_cpu_1_data), .Address(ecm_16_cpu_1_address), .IR(IR_disp), .r0_r3(R0_3), .r4_r7(R4_7),
    .SR(SR_disp), .MDB(MDB_disp), .PC(PC), .SP(SP), .FP(FP), .BP(BP), .MAB(MAB_disp), .IV(IV_disp),
    .Addr(Addr_disp), .States_disp(states), .CW_SEL(sel), .CW_EN(en), .CW_LATCH(latch));
  D_FF_AS Int (.Set(1'b0), .D(or_3_out), .C(not_9_out), .Clr(and_5_out), .Q(Int_q));  // open: nQ
  LED led_390 (.in(Int_q));
  LED F1 (.in(states[15]));
  LED F_Int (.in(states[13]));
  LED F2 (.in(states[14]));
  LED MAB_Load (.in(states[10]));
  LED SP_4 (.in(states[3]));
  LED ALU (.in(states[12]));
  LED MOV (.in(states[11]));
  LED LD_ST_MP (.in(states[9]));
  LED LD_ST_Direct (.in(states[8]));
  LED LDi (.in(states[7]));
  LED Addr_Arithm (.in(states[6]));
  LED Push_PC (.in(states[2]));
  LED Misc (.in(states[0]));
  LED MP_post (.in(states[5]));
  LED JMP (.in(states[4]));
  LED EINT (.in(states[1]));
  not not_10 (not_10_out, ecm_16_cpu_1_address[14]);
  and and_6 (and_6_out, not_10_out, read);
  _8K_word_RAM _8k_word_ram_1 (
    .Address(ecm_16_cpu_1_address[13:0]), .Single_byte(Byte), .CS(ecm_16_cpu_1_address[14]), .WE(write),
    .OE(read), .Data(ecm_16_cpu_1_data));
  LED led_391 (.in(sel[0]));
  LED led_392 (.in(sel[1]));
  LED led_393 (.in(sel[2]));
  LED led_394 (.in(sel[3]));
  LED led_395 (.in(sel[4]));
  LED led_396 (.in(sel[5]));
  LED led_397 (.in(sel[6]));
  LED led_398 (.in(sel[7]));
  LED led_399 (.in(sel[8]));
  LED led_400 (.in(sel[9]));
  LED led_401 (.in(sel[10]));
  LED led_402 (.in(sel[11]));
  LED led_403 (.in(sel[12]));
  LED led_404 (.in(sel[13]));
  LED led_405 (.in(sel[14]));
  LED led_406 (.in(sel[15]));
  ROM #(.AddrBits(7), .Bits(16)) ROM (.A(ecm_16_cpu_1_address[7:1]), .sel(not_10_out), .D(ROM_d));
  LED led_407 (.in(en[0]));
  LED led_408 (.in(en[1]));
  LED led_409 (.in(en[2]));
  LED led_410 (.in(en[3]));
  LED led_411 (.in(en[4]));
  LED led_412 (.in(en[5]));
  LED led_413 (.in(en[6]));
  LED led_414 (.in(en[7]));
  LED led_415 (.in(en[8]));
  assign ecm_16_cpu_1_data = and_6_out ? ROM_d : 16'bz;  // Driver driver_1
  LED led_416 (.in(latch[0]));
  LED led_417 (.in(latch[1]));
  LED led_418 (.in(latch[2]));
  LED led_419 (.in(latch[3]));
  LED led_420 (.in(latch[4]));
  LED led_421 (.in(latch[5]));
  LED led_422 (.in(latch[6]));
  LED led_423 (.in(latch[7]));
  LED led_424 (.in(latch[8]));
  LED led_425 (.in(latch[9]));

  // Notes on the sheet:
  //   Clk: Hz: 60
  //   in_3: from interrupt controller
  //   DMA_RQ: Request Direct Memory Access
  //   CPU Internal state display
  //   Registers display
  //   Z
  //   N
  //   O
  //   C
  //   Clock
  //   ECM-16/TTL Computer
  //   Fetch EINT === int ack
  //   Interrupt controller mock
  //   States display
  //   Data bus (16bit)
  //   Address bus (32bit)
  //   RAM is on addresses 0x4000 through 0x7FFF
  //   Memory subsystem
  //   Addr_MAB
  //   Addr_Direct
  //   LA3_0
  //   LA3_1
  //   ROM is on addresses 0x0000 through 0x00FE
  //   Control word
  //   S0
  //   S3_0
  //   S3_1
  //   S4
  //   S5
  //   S6
  //   S7
  //   S8
  //   S9_0
  //   S9_1
  //   S11
  //   S12
  //   contents of ROM (hex, n*v repeats v):
  //   2000,c,2100,2,e130,f009,3249,1100,16,1000,24,2100,4,e130,f009
  //   ,3369,1e00,e,1000,1a,8caa,d498,8caa,10ff,ffe4,8d33,d5b8,8d33,100
  //   ,8eff,d6d8,8eff,100,8ff7,d7f8,8f77,100
  //   E1
  //   E2
  //   E3
  //   E4
  //   E5
  //   E6
  //   E7
  //   T1
  //   T2
  //   L0
  //   L1
  //   L2
  //   L3
  //   L4
  //   L5
  //   L6
  //   L7
  //   L8
  //   W
endmodule
